// Logisim project CPU.circ as structural Verilog: 8 circuits, main circuit CPU
module main (
);

  wire clock_1_out, cpu_1_halt, frontpanelcontroller_1_cpuclk, frontpanelcontroller_1_runhalt, Reset_out,
       RunStop_out, Step_out;
  wire [3:0] cpu_1_aluflags, cpu_1_flags;
  wire [15:0] cpu_1_alua, cpu_1_alub, cpu_1_aluresult, cpu_1_dmaddress, cpu_1_dmdata, cpu_1_imaddress,
       cpu_1_imdata, cpu_1_writeback, IM_data;

  Clock clock_1 (.out(clock_1_out));
  ROM #(.addrWidth(16), .dataWidth(16)) IM (.addr(cpu_1_imaddress), .data(IM_data));
  FrontPanelController frontpanelcontroller_1 (
    .Clk(clock_1_out), .Run(RunStop_out), .Step(Step_out), .Reset(Reset_out), .Halt(cpu_1_halt),
    .CpuClk(frontpanelcontroller_1_cpuclk), .RunHalt(frontpanelcontroller_1_runhalt));
  CPU cpu_1 (
    .CLK(frontpanelcontroller_1_cpuclk), .Reset(Reset_out), .IMDataIn(IM_data), .Halt(cpu_1_halt),
    .IMAddress(cpu_1_imaddress), .IMData(cpu_1_imdata), .DMAddress(cpu_1_dmaddress), .DMData(cpu_1_dmdata),
    .WriteBack(cpu_1_writeback), .Flags(cpu_1_flags), .AluA(cpu_1_alua), .AluB(cpu_1_alub),
    .ALUResult(cpu_1_aluresult), .ALUFlags(cpu_1_aluflags));
  LED led_1 (.in(cpu_1_flags[3]));
  LED led_2 (.in(cpu_1_flags[2]));
  LED led_3 (.in(cpu_1_flags[1]));
  LED led_4 (.in(cpu_1_flags[0]));
  Hex_Digit_Display hex_digit_display_1 (.value(cpu_1_alua[15:12]));  // open: dp
  LED led_5 (.in(cpu_1_halt));
  Hex_Digit_Display hex_digit_display_2 (.value(cpu_1_imaddress[15:12]));  // open: dp
  Hex_Digit_Display hex_digit_display_3 (.value(cpu_1_imaddress[11:8]));  // open: dp
  Hex_Digit_Display hex_digit_display_4 (.value(cpu_1_imdata[15:12]));  // open: dp
  Hex_Digit_Display hex_digit_display_5 (.value(cpu_1_imdata[11:8]));  // open: dp
  Hex_Digit_Display hex_digit_display_6 (.value(cpu_1_alua[11:8]));  // open: dp
  Hex_Digit_Display hex_digit_display_7 (.value(cpu_1_alua[7:4]));  // open: dp
  LED N (.in(cpu_1_aluflags[3]));
  LED Z (.in(cpu_1_aluflags[2]));
  LED C (.in(cpu_1_aluflags[1]));
  LED led_6 (.in(frontpanelcontroller_1_runhalt));
  Button RunStop (.out(RunStop_out));
  Hex_Digit_Display hex_digit_display_8 (.value(cpu_1_imaddress[7:4]));  // open: dp
  Hex_Digit_Display hex_digit_display_9 (.value(cpu_1_imaddress[3:0]));  // open: dp
  Hex_Digit_Display hex_digit_display_10 (.value(cpu_1_imdata[7:4]));  // open: dp
  // Hex_Digit_Display hex_digit_display_11: pin names not known; wires that end beside it: cpu_1_imdata[3:0]
  Hex_Digit_Display hex_digit_display_12 (.value(cpu_1_alua[3:0]));  // open: dp
  LED V (.in(cpu_1_aluflags[0]));
  Button Step (.out(Step_out));
  Hex_Digit_Display hex_digit_display_13 (.value(cpu_1_dmaddress[15:12]));  // open: dp
  Hex_Digit_Display hex_digit_display_14 (.value(cpu_1_dmdata[15:12]));  // open: dp
  Hex_Digit_Display hex_digit_display_15 (.value(cpu_1_writeback[15:12]));  // open: dp
  Hex_Digit_Display hex_digit_display_16 (.value(cpu_1_alub[15:12]));  // open: dp
  Hex_Digit_Display hex_digit_display_17 (.value(cpu_1_aluresult[15:12]));  // open: dp
  Button Reset (.out(Reset_out));
  Hex_Digit_Display hex_digit_display_18 (.value(cpu_1_dmaddress[11:8]));  // open: dp
  Hex_Digit_Display hex_digit_display_19 (.value(cpu_1_dmaddress[7:4]));  // open: dp
  Hex_Digit_Display hex_digit_display_20 (.value(cpu_1_dmdata[11:8]));  // open: dp
  Hex_Digit_Display hex_digit_display_21 (.value(cpu_1_dmdata[7:4]));  // open: dp
  Hex_Digit_Display hex_digit_display_22 (.value(cpu_1_writeback[11:8]));  // open: dp
  Hex_Digit_Display hex_digit_display_23 (.value(cpu_1_writeback[7:4]));  // open: dp
  Hex_Digit_Display hex_digit_display_24 (.value(cpu_1_alub[11:8]));  // open: dp
  Hex_Digit_Display hex_digit_display_25 (.value(cpu_1_alub[7:4]));  // open: dp
  Hex_Digit_Display hex_digit_display_26 (.value(cpu_1_aluresult[11:8]));  // open: dp
  Hex_Digit_Display hex_digit_display_27 (.value(cpu_1_aluresult[7:4]));  // open: dp
  Hex_Digit_Display hex_digit_display_28 (.value(cpu_1_dmaddress[3:0]));  // open: dp
  Hex_Digit_Display hex_digit_display_29 (.value(cpu_1_dmdata[3:0]));  // open: dp
  Hex_Digit_Display hex_digit_display_30 (.value(cpu_1_writeback[3:0]));  // open: dp
  Hex_Digit_Display hex_digit_display_31 (.value(cpu_1_alub[3:0]));  // open: dp
  Hex_Digit_Display hex_digit_display_32 (.value(cpu_1_aluresult[3:0]));  // open: dp

  // Notes on the sheet:
  //   contents of IM (hex, n*v repeats v):
  //   e400 8000 1830 800f b000 10f3 1983 c001 21b4 18f3 b000 10f3 c001 23b4 18f3 11ab b000 c001 192b 8001
  //   9000 1011 b000 10f3 1993 c001 21b4 18f3 8001 b000 10f3 1983 c001 21b4 18f3 b000 10f3 c001 23b4 18f3
  //   1183 b000 10f3 c001 23b4 18f3 118b 2250 c00 9002 3611 c00 3611 b001 2c93 b000 10f3 1993 c001 21b4
  //   18f3 b000 10f3 c001 23b4 1183 2c00 60b0 8001 9000 1011 b000 10f3 1993 c001 21b4 18f3 b000 10f3 c001
  //   23b4 18f3 11ab 8000 9fff 1829 8001 9000 1011 b000 10f3 1993 c001 21b4 18f3 8001 b000 10f3 1983 c001
  //   21b4 18f3 b000 10f3 c001 23b4 18f3 1183 b000 10f3 c001 23b4 18f3 118b 2c50 b000 10f3 1993 c001 21b4
  //   18f3 b000 10f3 c001 23b4 1183 2c00 6047 8001 9000 1011 b000 10f3 1993 c001 21b4 18f3 8003 b000 10f3
  //   1983 c001 21b4 18f3 b000 10f3 c001 23b4 18f3 1183 b000 10f3 c001 23b4 18f3 118b 2450 b000 10f3 1993
  //   c001 21b4 18f3 8001 b000 10f3 1983 c001 21b4 18f3 b000 10f3 c001 23b4 18f3 1183 b000 10f3 c001 23b4
  //   18f3 118b 2050 b000 10f3 1993 c001 21b4 18f3 b000 10f3 c001 23b4 18f3 11ab b000 c001 192b 402c 8001
  //   9000 1011 b000 10f3 1993 c001 21b4 18f3 8001 b000 10f3 1983 c001 21b4 18f3 b000 10f3 c001 23b4 18f3
  //   1183 b000 10f3 c001 23b4 18f3 118b 3650 b000 10f3 1993 c001 21b4 18f3 b000 10f3 c001 23b4 18f3 11ab
  //   b000 c001 192b 4f1f 8001 9000 1011 b000 10f3 1993 c001 21b4 18f3 b000 10f3 c001 23b4 18f3 11ab 8000
  //   9fff 1829 600
  //   N  Z  C  V
  //   Latched Flags
  //   HALT
  //   Instruction Memory
  //   alARM
  //   ALU A Input
  //   ALU Flags
  //   Data Memory
  //   WriteBack
  //   ALU B Input
  //   ALU Result
endmodule

module CPU (
  input  CLK,
  input  Reset,
  input  [15:0] IMDataIn,
  output Halt,
  output [15:0] IMAddress,
  output [15:0] IMData,
  output [15:0] DMAddress,
  output [15:0] DMData,
  output [15:0] WriteBack,
  output [3:0] Flags,
  output [15:0] AluA,
  output [15:0] AluB,
  output [15:0] ALUResult,
  output [3:0] ALUFlags
);

  wire CLKin, d_ff_1_qn, decoder_control_1_carryin, decoder_control_1_flagw, decoder_control_1_jmp,
       decoder_control_1_memtoreg, decoder_control_1_memwrite, decoder_control_1_mov_flag,
       decoder_control_1_movr7, decoder_control_1_offset, decoder_control_1_regw,
       decoder_control_1_resultcheck, HaltCheck, or_1_out;
  wire [2:0] multiplexer_4_out, multiplexer_5_out;
  wire [3:0] ALUOp, decoder_control_1_latchflags, multiplexer_2_out;
  wire [15:0] bit_extender_1_out, bit_extender_2_out, datamemory_1_dmdataout, ifu_1_pcplus1,
       multiplexer_1_out, multiplexer_3_out, multiplexer_6_out, multiplexer_7_out, multiplexer_9_out,
       registerfile_1_rd2;

  Multiplexer #(.width(16)) multiplexer_1 (
    .in0(ALUResult), .in1(AluB), .out(multiplexer_1_out), .sel(decoder_control_1_movr7));
  Multiplexer #(.width(4)) multiplexer_2 (
    .in0(ALUFlags), .in1(AluA[3:0]), .out(multiplexer_2_out), .sel(decoder_control_1_mov_flag));
  IFU ifu_1 (
    .JMP(decoder_control_1_jmp), .CLK(CLKin), .Reset(Reset), .WBBus(multiplexer_1_out),
    .IMAddress(IMAddress), .PCPlus1(ifu_1_pcplus1));
  D_Flip_Flop #(.trigger("falling")) d_ff_1 (
    .D(HaltCheck), .clk(CLKin), .Q(Halt), .Qn(d_ff_1_qn), .reset(Reset));  // open: preset
  Multiplexer #(.width(16)) multiplexer_3 (
    .in0(AluA), .in1(ALUResult), .out(multiplexer_3_out), .sel(decoder_control_1_resultcheck));
  and and_1 (CLKin, d_ff_1_qn, CLK);
  Multiplexer #(.width(3)) multiplexer_4 (
    .in0(IMDataIn[5:3]), .in1(IMDataIn[14:12]), .out(multiplexer_4_out), .sel(IMDataIn[15]));
  Multiplexer #(.width(3)) multiplexer_5 (
    .in0(IMDataIn[8:6]), .in1(3'b111), .out(multiplexer_5_out), .sel(decoder_control_1_jmp));
  Multiplexer #(.width(16)) multiplexer_6 (
    .in0(multiplexer_3_out), .in1(AluB), .out(multiplexer_6_out), .sel(IMDataIn[15]));
  assign bit_extender_1_out = {{4{IMDataIn[11]}}, IMDataIn[11:0]};  // Bit_Extender bit_extender_1
  Decoder_Control decoder_control_1 (
    .IMData(IMDataIn[15:9]), .FlagsNZCV(multiplexer_2_out), .CLK(CLKin), .Reset(Reset), .ALUOp(ALUOp),
    .RegW(decoder_control_1_regw), .CarryIn(decoder_control_1_carryin),
    .LatchFlags(decoder_control_1_latchflags), .MemToReg(decoder_control_1_memtoreg),
    .JMP(decoder_control_1_jmp), .MovR7(decoder_control_1_movr7), .Halt(HaltCheck),
    .FlagW(decoder_control_1_flagw), .MOV_Flag(decoder_control_1_mov_flag),
    .ResultCheck(decoder_control_1_resultcheck), .Offset(decoder_control_1_offset),
    .MemWrite(decoder_control_1_memwrite));
  Multiplexer #(.width(16)) multiplexer_7 (
    .in0(multiplexer_6_out), .in1(bit_extender_2_out), .out(multiplexer_7_out), .sel(decoder_control_1_flagw));
  assign bit_extender_2_out = {{12{1'b0}}, decoder_control_1_latchflags};  // Bit_Extender bit_extender_2
  Multiplexer #(.width(16)) multiplexer_8 (
    .in0(multiplexer_7_out), .in1(datamemory_1_dmdataout), .out(WriteBack), .sel(decoder_control_1_memtoreg));
  RegisterFile registerfile_1 (
    .CLK(CLKin), .WE3(decoder_control_1_regw), .A1(multiplexer_5_out), .A2(IMDataIn[2:0]),
    .A3(multiplexer_4_out), .WD3(WriteBack), .R7(ifu_1_pcplus1), .Reset(Reset), .RD1(AluA),
    .RD2(registerfile_1_rd2), .RD3(DMData));
  ALU alu_1 (
    .A(AluA), .B(AluB), .CarryIn(decoder_control_1_carryin), .ALUOp(ALUOp), .Result(ALUResult),
    .FlagsNZCV(ALUFlags));
  Multiplexer #(.width(16)) multiplexer_9 (
    .in0({16{1'b0}}), .in1(registerfile_1_rd2), .out(multiplexer_9_out), .sel(decoder_control_1_offset));
  or or_1 (or_1_out, IMDataIn[15], decoder_control_1_jmp);
  Multiplexer #(.width(16)) multiplexer_10 (
    .in0(multiplexer_9_out), .in1(bit_extender_1_out), .out(AluB), .sel(or_1_out));
  DataMemory datamemory_1 (
    .DmAddress(ALUResult), .WE(decoder_control_1_memwrite), .CLK(CLKin), .DMDataIn(DMData),
    .DMDataOut(datamemory_1_dmdataout));

  assign DMAddress = ALUResult;
  assign IMData = IMDataIn;

  // Other names for the same wires on the sheet: A[15:0] = AluA; B[15:0] = AluB; Result[15:0] = ALUResult

  // Notes on the sheet:
  //   Build your CPU here
endmodule

module FrontPanelController (
  input  Clk,
  input  Run,
  input  Step,
  input  Reset,
  input  Halt,
  output CpuClk,
  output RunHalt
);

  wire and_1_out, or_1_out, pull_resistor_1_node, t_ff_1_q;

  T_Flip_Flop t_ff_1 (.T(pull_resistor_1_node), .clk(Run), .Q(t_ff_1_q), .reset(Reset));  // open: Qn, preset
  Pull_Resistor #(.pull(1)) pull_resistor_1 (.node(pull_resistor_1_node));
  or or_1 (or_1_out, t_ff_1_q, Step);
  and and_1 (and_1_out, Clk, t_ff_1_q);
  and and_2 (RunHalt, or_1_out, ~Halt);  // AND_Gate
  Multiplexer multiplexer_1 (.in0(Step), .in1(and_1_out), .out(CpuClk), .sel(t_ff_1_q));
endmodule

module ALU (
  input  [15:0] A,
  input  [15:0] B,
  input  CarryIn,
  input  [3:0] ALUOp,
  output [15:0] Result,
  output [3:0] FlagsNZCV
);

  wire adder_1_cout, and_2_out, and_4_out, multiplexer_3_out, nand_1_out, not_2_out, or_2_out,
       subtractor_1_bout, xnor_1_out, xor_2_out;
  wire [15:0] adder_1_out, and_1_out, divider_1_out, divider_1_rem, multiplexer_2_out, multiplier_1_cout,
       multiplier_1_out, not_1_out, or_1_out, shifter_1_out, shifter_2_out, shifter_3_out, shifter_4_out,
       shifter_5_out, subtractor_1_out, xor_1_out;

  Adder #(.width(16)) adder_1 (.a(A), .b(B), .out(adder_1_out), .cout(adder_1_cout));  // open: cin
  Subtractor #(.width(16)) subtractor_1 (.a(A), .b(B), .out(subtractor_1_out), .bout(subtractor_1_bout));  // open: bin
  Multiplier #(.width(16)) multiplier_1 (.a(A), .b(B), .out(multiplier_1_out), .cout(multiplier_1_cout));  // open: cin
  Divider #(.width(16)) divider_1 (.a(A), .b(B), .out(divider_1_out), .rem(divider_1_rem));  // open: upper
  assign and_1_out = A & B;  // AND_Gate and_1, 16 bits wide
  assign or_1_out = A | B;  // OR_Gate or_1, 16 bits wide
  assign xor_1_out = A ^ B;  // XOR_Gate xor_1, 16 bits wide
  assign not_1_out = ~A;  // NOT_Gate not_1, 16 bits wide
  Shifter #(.width(16)) shifter_1 (.in(A), .\dist (B[3:0]), .out(shifter_1_out));
  Shifter #(.shift("lr"), .width(16)) shifter_2 (.in(A), .\dist (B[3:0]), .out(shifter_2_out));
  Shifter #(.shift("ar"), .width(16)) shifter_3 (.in(A), .\dist (B[3:0]), .out(shifter_3_out));
  Shifter #(.shift("rl"), .width(16)) shifter_4 (.in(A), .\dist (B[3:0]), .out(shifter_4_out));
  Shifter #(.shift("rr"), .width(16)) shifter_5 (.in(A), .\dist (B[3:0]), .out(shifter_5_out));
  Multiplexer #(.select(4), .width(16)) multiplexer_1 (
    .in0(adder_1_out), .in1(subtractor_1_out), .in2(multiplier_1_out), .in3(multiplier_1_cout),
    .in4(divider_1_out), .in5(divider_1_rem), .in6(and_1_out), .in7(or_1_out), .in8(xor_1_out),
    .in9(not_1_out), .in10(shifter_1_out), .in11(shifter_2_out), .in12(shifter_3_out), .in13(shifter_4_out),
    .in14(shifter_5_out), .in15(subtractor_1_out), .out({FlagsNZCV[3], Result[14:0]}), .sel(ALUOp));
  Multiplexer #(.width(16)) multiplexer_2 (
    .in0(adder_1_out), .in1(subtractor_1_out), .out(multiplexer_2_out), .sel(ALUOp[0]));
  Multiplexer multiplexer_3 (.in0(adder_1_cout), .in1(subtractor_1_bout), .out(multiplexer_3_out), .sel(ALUOp[0]));
  NotExactlyOne xnor_1 (.out(xnor_1_out), .in0(A[15]), .in1(B[15]), .in2(ALUOp[0]));
  xor xor_2 (xor_2_out, B[15], multiplexer_2_out[15]);
  nor nor_1 (FlagsNZCV[2], FlagsNZCV[3], Result[14], Result[13], Result[12], Result[11], Result[10], Result[9], Result[8], Result[7], Result[6], Result[5], Result[4], Result[3], Result[2], Result[1], Result[0]);
  nand nand_1 (nand_1_out, ALUOp[3], ALUOp[2], ALUOp[1]);
  or or_2 (or_2_out, multiplier_1_out[0], multiplier_1_out[1], multiplier_1_out[2], multiplier_1_out[3], multiplier_1_out[4], multiplier_1_out[5], multiplier_1_out[6], multiplier_1_out[7], multiplier_1_out[8], multiplier_1_out[9], multiplier_1_out[10], multiplier_1_out[11], multiplier_1_out[12], multiplier_1_out[13], multiplier_1_out[14], multiplier_1_out[15]);
  and and_2 (and_2_out, xnor_1_out, xor_2_out, nand_1_out);
  and and_3 (FlagsNZCV[1], nand_1_out, multiplexer_3_out);
  not not_2 (not_2_out, ALUOp[1]);
  and and_4 (and_4_out, ALUOp[3], ALUOp[2], not_2_out, ALUOp[0], or_2_out);
  or or_3 (FlagsNZCV[0], and_4_out, and_2_out, CarryIn);

  assign Result[15] = FlagsNZCV[3];
endmodule

module IFU (
  input  JMP,
  input  CLK,
  input  Reset,
  input  [15:0] WBBus,
  output [15:0] IMAddress,
  output [15:0] PCPlus1
);

  wire [15:0] multiplexer_1_out;

  Register #(.width(16)) R7 (.D(multiplexer_1_out), .clk(CLK), .Q(IMAddress), .clr(Reset));  // open: en
  Multiplexer #(.width(16)) multiplexer_1 (.in0(PCPlus1), .in1(WBBus), .out(multiplexer_1_out), .sel(JMP));
  Adder #(.width(16)) adder_1 (.a(IMAddress), .b(16'h1), .out(PCPlus1));  // open: cin, cout
endmodule

module RegisterFile (
  input  CLK,
  input  WE3,
  input  [2:0] A1,
  input  [2:0] A2,
  input  [2:0] A3,
  input  [15:0] WD3,
  input  [15:0] R7,
  input  Reset,
  output [15:0] RD1,
  output [15:0] RD2,
  output [15:0] RD3
);

  wire demultiplexer_1_out0, demultiplexer_1_out1, demultiplexer_1_out2, demultiplexer_1_out3,
       demultiplexer_1_out4, demultiplexer_1_out5, demultiplexer_1_out6;
  wire [15:0] R0_q, R1_q, R2_q, R3_q, R4_q, R5_q, R6_q;

  Demultiplexer #(.select(3)) demultiplexer_1 (
    .out0(demultiplexer_1_out0), .out1(demultiplexer_1_out1), .out2(demultiplexer_1_out2),
    .out3(demultiplexer_1_out3), .out4(demultiplexer_1_out4), .out5(demultiplexer_1_out5),
    .out6(demultiplexer_1_out6), .in(WE3), .sel(A3));  // open: out7
  Register #(.width(16)) R0 (.D(WD3), .en(demultiplexer_1_out0), .clk(CLK), .Q(R0_q), .clr(Reset));
  Register #(.width(16)) R1 (.D(WD3), .en(demultiplexer_1_out1), .clk(CLK), .Q(R1_q), .clr(Reset));
  Register #(.width(16)) R2 (.D(WD3), .en(demultiplexer_1_out2), .clk(CLK), .Q(R2_q), .clr(Reset));
  Register #(.width(16)) R3 (.D(WD3), .en(demultiplexer_1_out3), .clk(CLK), .Q(R3_q), .clr(Reset));
  Register #(.width(16)) R4 (.D(WD3), .en(demultiplexer_1_out4), .clk(CLK), .Q(R4_q), .clr(Reset));
  Register #(.width(16)) R5 (.D(WD3), .en(demultiplexer_1_out5), .clk(CLK), .Q(R5_q), .clr(Reset));
  Register #(.width(16)) R6 (.D(WD3), .en(demultiplexer_1_out6), .clk(CLK), .Q(R6_q), .clr(Reset));
  Multiplexer #(.select(3), .width(16)) multiplexer_1 (
    .in0(R0_q), .in1(R1_q), .in2(R2_q), .in3(R3_q), .in4(R4_q), .in5(R5_q), .in6(R6_q), .in7(R7), .out(RD1),
    .sel(A1));
  Multiplexer #(.select(3), .width(16)) multiplexer_2 (
    .in0(R0_q), .in1(R1_q), .in2(R2_q), .in3(R3_q), .in4(R4_q), .in5(R5_q), .in6(R6_q), .in7(R7), .out(RD2),
    .sel(A2));
  Multiplexer #(.select(3), .width(16)) multiplexer_3 (
    .in0(R0_q), .in1(R1_q), .in2(R2_q), .in3(R3_q), .in4(R4_q), .in5(R5_q), .in6(R6_q), .in7(R7), .out(RD3),
    .sel(A3));

  // Other names for the same wires on the sheet: R = Reset
endmodule

module DataMemory (
  input  [15:0] DmAddress,
  input  WE,
  input  CLK,
  input  [15:0] DMDataIn,
  output [15:0] DMDataOut
);

  RAM #(.addrWidth(16), .asyncread("true"), .dataWidth(16)) ram_1 (
    .addr(DmAddress), .we(WE), .clk(CLK), .din(DMDataIn), .dout(DMDataOut));  // open: oe
endmodule

module Decoder_Control (
  input  [6:0] IMData,
  input  [3:0] FlagsNZCV,
  input  CLK,
  input  Reset,
  output [3:0] ALUOp,
  output RegW,
  output CarryIn,
  output [3:0] LatchFlags,
  output MemToReg,
  output JMP,
  output MovR7,
  output Halt,
  output FlagW,
  output MOV_Flag,
  output ResultCheck,
  output Offset,
  output MemWrite
);

  wire and_2_out, and_3_out, and_4_out, and_9_out, and_10_out, and_11_out, and_12_out, and_13_out,
       and_14_out, and_15_out, and_16_out, and_17_out, and_18_out, and_19_out, not_1_out, not_2_out,
       not_3_out, not_4_out, not_5_out, not_6_out, not_7_out, not_8_out, not_9_out, not_10_out, not_11_out,
       not_12_out, not_13_out, not_14_out, not_15_out, not_16_out, not_17_out, not_18_out, not_19_out,
       not_20_out, not_21_out, not_22_out, not_23_out, not_24_out, not_25_out, not_26_out, not_27_out,
       not_28_out, not_29_out, not_30_out, not_31_out, not_32_out, not_33_out, not_34_out, not_35_out,
       not_36_out, not_37_out, not_38_out, not_39_out, not_40_out, not_41_out, not_42_out, not_43_out,
       not_44_out, not_45_out, not_46_out, not_47_out, not_48_out, not_49_out, not_50_out, not_51_out,
       not_52_out, not_53_out, not_54_out, not_55_out, not_56_out, not_57_out, not_58_out, not_59_out,
       not_60_out, not_61_out, not_62_out, not_63_out, or_1_out, or_2_out, or_4_out, or_8_out;

  or or_1 (or_1_out, ResultCheck, MOV_Flag);
  Register #(.width(4)) register_1 (
    .D(FlagsNZCV), .en(or_1_out), .clk(CLK), .Q({LatchFlags[3:2], CarryIn, LatchFlags[0]}), .clr(Reset));
  not not_1 (not_1_out, IMData[6]);
  and and_1 (ResultCheck, not_1_out, not_2_out, IMData[4]);
  not not_2 (not_2_out, IMData[5]);
  not not_3 (not_3_out, IMData[5]);
  not not_4 (not_4_out, IMData[6]);
  not not_5 (not_5_out, IMData[6]);
  and and_2 (and_2_out, not_5_out, IMData[5], not_6_out);
  not not_6 (not_6_out, IMData[4]);
  not not_7 (not_7_out, IMData[6]);
  and and_3 (and_3_out, not_7_out, IMData[5], IMData[4], not_8_out, LatchFlags[2]);
  not not_8 (not_8_out, IMData[3]);
  not not_9 (not_9_out, IMData[6]);
  and and_4 (and_4_out, not_9_out, IMData[5], IMData[4], IMData[3], not_10_out);
  not not_10 (not_10_out, LatchFlags[2]);
  and and_5 (MovR7, IMData[6], IMData[5], IMData[4], IMData[3]);
  not not_11 (not_11_out, IMData[6]);
  not not_12 (not_12_out, IMData[5]);
  not not_13 (not_13_out, IMData[4]);
  not not_14 (not_14_out, IMData[3]);
  and and_6 (Halt, not_11_out, not_12_out, not_13_out, not_14_out, not_15_out, IMData[1], IMData[0]);
  not not_15 (not_15_out, IMData[2]);
  not not_16 (not_16_out, IMData[6]);
  not not_17 (not_17_out, IMData[5]);
  not not_18 (not_18_out, IMData[4]);
  not not_19 (not_19_out, IMData[3]);
  and and_7 (FlagW, not_16_out, not_17_out, not_18_out, not_19_out, IMData[2], IMData[1], not_20_out);
  not not_20 (not_20_out, IMData[0]);
  not not_21 (not_21_out, IMData[6]);
  not not_22 (not_22_out, IMData[5]);
  not not_23 (not_23_out, IMData[4]);
  not not_24 (not_24_out, IMData[3]);
  and and_8 (MOV_Flag, not_21_out, not_22_out, not_23_out, not_24_out, IMData[2], IMData[1], IMData[0]);
  not not_25 (not_25_out, IMData[6]);
  not not_26 (not_26_out, IMData[5]);
  not not_27 (not_27_out, IMData[4]);
  and and_9 (and_9_out, not_25_out, not_26_out, not_27_out, IMData[3], not_28_out, IMData[1], IMData[0]);
  not not_28 (not_28_out, IMData[2]);
  not not_29 (not_29_out, IMData[6]);
  not not_30 (not_30_out, IMData[5]);
  not not_31 (not_31_out, IMData[4]);
  and and_10 (and_10_out, not_29_out, not_30_out, not_31_out, IMData[3], IMData[2], IMData[1], IMData[0]);
  not not_32 (not_32_out, IMData[6]);
  not not_33 (not_33_out, IMData[5]);
  not not_34 (not_34_out, IMData[4]);
  and and_11 (and_11_out, not_32_out, not_33_out, not_34_out, IMData[3], IMData[2], not_35_out, not_36_out);
  not not_35 (not_35_out, IMData[1]);
  not not_36 (not_36_out, IMData[0]);
  and and_12 (and_12_out, IMData[4], not_3_out, not_4_out);
  not not_37 (not_37_out, IMData[6]);
  not not_38 (not_38_out, IMData[5]);
  and and_13 (and_13_out, not_37_out, not_38_out, IMData[4], IMData[3], IMData[2], IMData[1], IMData[0]);
  not not_39 (not_39_out, IMData[6]);
  not not_40 (not_40_out, IMData[5]);
  not not_41 (not_41_out, IMData[4]);
  not not_42 (not_42_out, IMData[3]);
  and and_14 (and_14_out, not_39_out, not_40_out, not_41_out, not_42_out, IMData[2], not_43_out, not_44_out);
  not not_43 (not_43_out, IMData[1]);
  not not_44 (not_44_out, IMData[0]);
  not not_45 (not_45_out, IMData[6]);
  not not_46 (not_46_out, IMData[5]);
  not not_47 (not_47_out, IMData[4]);
  not not_48 (not_48_out, IMData[3]);
  and and_15 (and_15_out, not_45_out, not_46_out, not_47_out, not_48_out, IMData[2], IMData[1], not_49_out);
  not not_49 (not_49_out, IMData[0]);
  not not_50 (not_50_out, IMData[6]);
  not not_51 (not_51_out, IMData[5]);
  not not_52 (not_52_out, IMData[4]);
  and and_16 (and_16_out, not_50_out, not_51_out, not_52_out, IMData[3], not_53_out, not_54_out, not_55_out);
  not not_53 (not_53_out, IMData[2]);
  not not_54 (not_54_out, IMData[1]);
  not not_55 (not_55_out, IMData[0]);
  not not_56 (not_56_out, IMData[6]);
  not not_57 (not_57_out, IMData[5]);
  not not_58 (not_58_out, IMData[4]);
  and and_17 (and_17_out, not_56_out, not_57_out, not_58_out, IMData[3], not_59_out, IMData[1], IMData[0]);
  not not_59 (not_59_out, IMData[2]);
  or or_2 (or_2_out, and_12_out, IMData[6]);
  and and_18 (and_18_out, or_2_out, not_60_out);
  not not_60 (not_60_out, and_13_out);
  or or_3 (MemToReg, and_16_out, and_17_out);
  or or_4 (or_4_out, and_2_out, and_3_out, and_4_out);
  nor nor_1 (Offset, and_9_out, and_10_out);
  or or_5 (MemWrite, and_10_out, and_11_out);
  or or_6 (JMP, or_4_out, MovR7);
  or or_7 (RegW, and_18_out, and_14_out, and_15_out, MemToReg);
  not not_61 (not_61_out, IMData[6]);
  not not_62 (not_62_out, IMData[5]);
  not not_63 (not_63_out, IMData[4]);
  or or_8 (or_8_out, and_19_out, JMP);
  and and_19 (and_19_out, not_61_out, not_62_out, not_63_out, IMData[3]);
  Multiplexer #(.width(4)) multiplexer_1 (.in0(IMData[3:0]), .in1(4'b0000), .out(ALUOp), .sel(or_8_out));

  assign LatchFlags[1] = CarryIn;
endmodule
